// Digital circuit VCU.dig as structural Verilog
module VCU (
  input  clk
);

  wire and_1_out, and_2_out, and_3_out, button_1_out, H_COUNTER_DEC, H_COUNTER_L, H_COUNTER_ovf, H_EN, H_L,
       JMP, JNZ_W, JZ_H, JZ_OAM, not_1_out, not_2_out, OAM_EN, OAM_MAR_CL, OAM_MAR_INC, or_1_out,
       VGA_BUFFER_L, VMAR_INC, VMAR_L, VRAM_EN, W_COUNTER_DEC, W_COUNTER_L, W_COUNTER_ovf, W_EN, W_L,
       X_COUNTER_INC, X_COUNTER_L, X_EN, X_L, Y_COUNTER_INC, Y_COUNTER_L, Y_EN, Y_L;
  wire [4:0] dipswitch_33_out, VPROM_d, VPROM_PC_out;
  wire [7:0] VGA_BUFFER_d, VRAM_d;
  wire [9:0] driver_3_out, driver_4_out, H_q, OAM_d, W_q, X_COUNTER_out, X_q, Y_COUNTER_out, Y_q;
  wire [15:0] VMAR_out;
  wire [15:10] OAM_d_2;
  wire [19:0] OAM_MAR_out;
  wire [31:0] dipswitch_1_out;

  RAMDualPort #(.AddrBits(20), .Bits(8)) VRAM (
    .A({4'b0000, VMAR_out}), .Din({8{1'b0}}), .str(1'b0), .C(clk), .ld(VRAM_EN), .D(VRAM_d));
  ROM #(.AddrBits(20), .Bits(16)) OAM (.A(OAM_MAR_out), .sel(OAM_EN), .D({OAM_d_2, OAM_d}));
  Button button_1 (.out(button_1_out));
  Register #(.Bits(10)) X (.D(OAM_d), .C(X_L), .en(X_L), .Q(X_q));
  Register #(.Bits(10)) Y (.D(OAM_d), .C(Y_L), .en(Y_L), .Q(Y_q));
  CounterPreset #(.Bits(16)) VMAR (
    .en(VMAR_INC), .C(clk), .dir(1'b0), .in({OAM_d_2, OAM_d}), .ld(VMAR_L), .clr(1'b0), .out(VMAR_out));  // open: ovf
  CounterPreset #(.Bits(5)) VPROM_PC (
    .en(clk), .C(clk), .dir(1'b0), .in(VPROM_d), .ld(or_1_out), .clr(button_1_out), .out(VPROM_PC_out));  // open: ovf
  assign OAM_d = X_EN ? X_q : 10'bz;  // Driver driver_1
  assign OAM_d = Y_EN ? Y_q : 10'bz;  // Driver driver_2
  or or_1 (or_1_out, and_3_out, and_2_out, JMP, and_1_out);
  ROM #(.AddrBits(5), .isProgramMemory("true"), .Bits(32)) VPROM (
    .A(VPROM_PC_out), .sel(1'b1),
    .D({VPROM_d, JMP, JZ_H, JZ_OAM, JNZ_W, Y_EN, X_EN, H_EN, W_EN, Y_COUNTER_INC, H_COUNTER_DEC, VMAR_INC, X_COUNTER_INC, W_COUNTER_DEC, VGA_BUFFER_L, VRAM_EN, VMAR_L, H_COUNTER_L, H_L, W_COUNTER_L, W_L, Y_COUNTER_L, Y_L, X_COUNTER_L, X_L, OAM_MAR_INC, OAM_EN, OAM_MAR_CL}));
  and and_1 (and_1_out, JZ_OAM, not_1_out);
  and and_2 (and_2_out, JNZ_W, not_2_out);
  and and_3 (and_3_out, H_COUNTER_ovf, JZ_H);
  CounterPreset #(.Bits(10)) X_COUNTER (
    .en(X_COUNTER_INC), .C(clk), .dir(1'b0), .in(OAM_d), .ld(X_COUNTER_L), .clr(1'b0), .out(X_COUNTER_out));  // open: ovf
  CounterPreset #(.Bits(10)) Y_COUNTER (
    .en(Y_COUNTER_INC), .C(clk), .dir(1'b0), .in(OAM_d), .ld(Y_COUNTER_L), .clr(1'b0), .out(Y_COUNTER_out));  // open: ovf
  not not_1 (not_1_out, OAM_d_2[15]);
  CounterPreset #(.Bits(20)) OAM_MAR (
    .en(OAM_MAR_INC), .C(clk), .dir(1'b0), .in({20{1'b0}}), .ld(1'b0), .clr(OAM_MAR_CL), .out(OAM_MAR_out));  // open: ovf
  not not_2 (not_2_out, W_COUNTER_ovf);
  Register #(.Bits(10)) W (.D(OAM_d), .C(W_L), .en(W_L), .Q(W_q));
  Register #(.Bits(10)) H (.D(OAM_d), .C(H_L), .en(H_L), .Q(H_q));
  assign driver_3_out = W_EN ? W_q : 10'bz;  // Driver driver_3
  assign driver_4_out = H_EN ? H_q : 10'bz;  // Driver driver_4
  assign driver_3_out = ~W_EN ? OAM_d : 10'bz;  // DriverInvSel driverinvsel_1
  // Probe on OAM_MAR_out
  // Probe on VPROM_PC_out
  // Probe on VMAR_out
  // Probe on {VPROM_d, JMP, JZ_H, JZ_OAM, JNZ_W, Y_EN, X_EN, H_EN, W_EN, Y_COUNTER_INC, H_COUNTER_DEC, VMAR_INC, X_COUNTER_INC, W_COUNTER_DEC, VGA_BUFFER_L, VRAM_EN, VMAR_L, H_COUNTER_L, H_L, W_COUNTER_L, W_L, Y_COUNTER_L, Y_L, X_COUNTER_L, X_L, OAM_MAR_INC, OAM_EN, OAM_MAR_CL}
  // Probe on VPROM_d
  // Probe on {OAM_d_2, OAM_d}
  // Probe on or_1_out
  CounterPreset #(.Bits(10)) W_COUNTER (
    .en(W_COUNTER_DEC), .C(clk), .dir(1'b1), .in(driver_3_out), .ld(W_COUNTER_L), .clr(1'b0),
    .ovf(W_COUNTER_ovf));  // open: out
  CounterPreset #(.Bits(10)) H_COUNTER (
    .en(H_COUNTER_DEC), .C(clk), .dir(1'b1), .in(driver_4_out), .ld(H_COUNTER_L), .clr(1'b0),
    .ovf(H_COUNTER_ovf));  // open: out
  DipSwitch dipswitch_1 (.out(dipswitch_1_out[0]));
  DipSwitch dipswitch_2 (.out(dipswitch_1_out[1]));
  DipSwitch dipswitch_3 (.out(dipswitch_1_out[2]));
  DipSwitch dipswitch_4 (.out(dipswitch_1_out[3]));
  DipSwitch dipswitch_5 (.out(dipswitch_1_out[4]));
  DipSwitch dipswitch_6 (.out(dipswitch_1_out[5]));
  DipSwitch dipswitch_7 (.out(dipswitch_1_out[6]));
  DipSwitch dipswitch_8 (.out(dipswitch_1_out[7]));
  DipSwitch dipswitch_9 (.out(dipswitch_1_out[8]));
  DipSwitch dipswitch_10 (.out(dipswitch_1_out[9]));
  DipSwitch dipswitch_11 (.out(dipswitch_1_out[10]));
  DipSwitch dipswitch_12 (.out(dipswitch_1_out[11]));
  DipSwitch dipswitch_13 (.out(dipswitch_1_out[12]));
  DipSwitch dipswitch_14 (.out(dipswitch_1_out[13]));
  DipSwitch dipswitch_15 (.out(dipswitch_1_out[14]));
  DipSwitch dipswitch_16 (.out(dipswitch_1_out[15]));
  DipSwitch dipswitch_17 (.out(dipswitch_1_out[16]));
  DipSwitch dipswitch_18 (.out(dipswitch_1_out[17]));
  DipSwitch dipswitch_19 (.out(dipswitch_1_out[18]));
  DipSwitch dipswitch_20 (.out(dipswitch_1_out[19]));
  DipSwitch dipswitch_21 (.out(dipswitch_1_out[20]));
  DipSwitch dipswitch_22 (.out(dipswitch_1_out[21]));
  DipSwitch dipswitch_23 (.out(dipswitch_1_out[22]));
  DipSwitch dipswitch_24 (.out(dipswitch_1_out[23]));
  DipSwitch dipswitch_25 (.out(dipswitch_1_out[24]));
  DipSwitch dipswitch_26 (.out(dipswitch_1_out[25]));
  DipSwitch dipswitch_27 (.out(dipswitch_1_out[26]));
  DipSwitch dipswitch_28 (.out(dipswitch_1_out[27]));
  DipSwitch dipswitch_29 (.out(dipswitch_1_out[28]));
  DipSwitch dipswitch_30 (.out(dipswitch_1_out[29]));
  DipSwitch dipswitch_31 (.out(dipswitch_1_out[30]));
  DipSwitch dipswitch_32 (.out(dipswitch_1_out[31]));
  RAMDualPort #(.AddrBits(20), .Bits(8)) VGA_BUFFER (
    .A({Y_COUNTER_out, X_COUNTER_out}), .Din(VRAM_d), .str(VGA_BUFFER_L), .C(clk), .ld(1'b0), .D(VGA_BUFFER_d));
  DipSwitch dipswitch_33 (.out(dipswitch_33_out[0]));
  DipSwitch dipswitch_34 (.out(dipswitch_33_out[1]));
  DipSwitch dipswitch_35 (.out(dipswitch_33_out[2]));
  DipSwitch dipswitch_36 (.out(dipswitch_33_out[3]));
  DipSwitch dipswitch_37 (.out(dipswitch_33_out[4]));
  Register #(.Bits(32)) register_1 (.D(dipswitch_1_out), .C(1'b1), .en(1'b1));  // open: Q

  // Notes on the sheet:
  //   contents of OAM (hex, n*v repeats v):
  //   8008,c,10,cc,23,30
  //   contents of VPROM (hex, n*v repeats v):
  //   3,fa00001e,66,186,606,1802,3081c000,31280110,0,0,0,0,0,0,0,0,0,0,0,0,0,0,0,0,0,0,
  //   0,0,0,0,0,f9000000
  //   OAM-MAR
  //   micro OP counter
  //   VMAR
  //   VPROM
  //   Jump address
  //   D-BUS
  //   Jump? 0= no, 1 = yes
endmodule
