// Digital circuit tellertje.dig as structural Verilog
module tellertje (
  input  clk
);

  wire _7411_1_pin6, _7411_1_pin8, _7411_1_pin11, _7411_1_pin12, _7421_1_pin6, _7421_1_pin8, _7421_1_pin9,
       _7421_2_pin6, _7421_2_pin8, _7486_1_pin3, _7486_1_pin6, _7486_1_pin8, _7486_1_pin11, _74163_1_pin1,
       _74163_1_pin15, _74163_2_pin1, _74163_2_pin10, _74163_2_pin15, _74163_3_pin15, _74163_4_pin15,
       and_1_out, and_2_out, and_3_out, d_ff_1_nq, d_ff_1_q, not_3_out, not_4_out, q0, q1, q2, q3, q4, q5,
       q6, q7, q8, q9, rs_ff_as_2_q, rs_ff_as_3_q, rs_ff_as_4_q, rs_ff_as_6_q, y0, y1, y2, y3, y4, y5, y6,
       y7, y8, y9;
  wire [7:0] _74157_1_pin7, RAM2_d, ramdualport_1_d, register_1_q, register_2_q;

  _74163 _74163_1 (
    .pin1(_74163_1_pin1), .pin2(clk), .pin3(1'b0), .pin4(1'b0), .pin5(1'b0), .pin6(1'b0), .pin7(1'b1),
    .pin8(1'b0), .pin9(1'b1), .pin10(1'b1), .pin11(q3), .pin12(q2), .pin13(q1), .pin14(q0),
    .pin15(_74163_1_pin15), .pin16(1'b1));
  _74163 _74163_2 (
    .pin1(_74163_2_pin1), .pin2(clk), .pin3(1'b0), .pin4(1'b0), .pin5(1'b0), .pin6(1'b0), .pin7(1'b1),
    .pin8(1'b0), .pin9(1'b1), .pin10(_74163_2_pin10), .pin11(y3), .pin12(y2), .pin13(y1), .pin14(y0),
    .pin15(_74163_2_pin15), .pin16(1'b1));
  // Probe on {q9, q8, q7, q6, q5, q4, q3, q2, q1, q0}
  // Probe on {y9, y8, y7, y6, y5, y4, y3, y2, y1, y0}
  _74163 _74163_3 (
    .pin1(_74163_1_pin1), .pin2(clk), .pin3(1'b0), .pin4(1'b0), .pin5(1'b0), .pin6(1'b0), .pin7(1'b1),
    .pin8(1'b0), .pin9(1'b1), .pin10(_74163_1_pin15), .pin11(q7), .pin12(q6), .pin13(q5), .pin14(q4),
    .pin15(_74163_3_pin15), .pin16(1'b1));
  _74163 _74163_4 (
    .pin1(_74163_2_pin1), .pin2(clk), .pin3(1'b0), .pin4(1'b0), .pin5(1'b0), .pin6(1'b0), .pin7(1'b1),
    .pin8(1'b0), .pin9(1'b1), .pin10(_74163_2_pin15), .pin11(y7), .pin12(y6), .pin13(y5), .pin14(y4),
    .pin15(_74163_4_pin15), .pin16(1'b1));
  _7421 _7421_1 (
    .pin1(y5), .pin2(y6), .pin4(y7), .pin5(y8), .pin6(_7421_1_pin6), .pin7(1'b0), .pin8(_7421_1_pin8),
    .pin9(_7421_1_pin9), .pin10(y1), .pin12(y3), .pin13(1'b1), .pin14(1'b1));  // open: pin3, pin11
  _7421 _7421_2 (
    .pin1(y9), .pin2(y0), .pin4(y2), .pin5(y3), .pin6(_7421_2_pin6), .pin7(1'b0), .pin8(_7421_2_pin8),
    .pin9(_7421_1_pin9), .pin10(1'b1), .pin12(y2), .pin13(y3), .pin14(1'b1));  // open: pin3, pin11
  _74163 _74163_5 (
    .pin1(_74163_1_pin1), .pin2(clk), .pin3(1'b0), .pin4(1'b0), .pin5(1'b0), .pin6(1'b0), .pin7(1'b1),
    .pin8(1'b0), .pin9(1'b1), .pin10(_74163_3_pin15), .pin13(q9), .pin14(q8), .pin16(1'b1));  // open: pin11, pin12, pin15
  _7411 _7411_1 (
    .pin1(q7), .pin2(q9), .pin3(q7), .pin4(q9), .pin5(q4), .pin6(_7411_1_pin6), .pin7(1'b0),
    .pin8(_7411_1_pin8), .pin9(q6), .pin10(q5), .pin11(_7411_1_pin11), .pin12(_7411_1_pin12), .pin13(1'b1),
    .pin14(1'b1));
  _7411 _7411_2 (
    .pin1(1'b0), .pin2(1'b0), .pin3(q5), .pin4(q9), .pin5(q8), .pin6(_74163_2_pin10), .pin7(1'b0),
    .pin9(1'b0), .pin10(1'b0), .pin11(1'b0), .pin13(1'b0), .pin14(1'b1));  // open: pin8, pin12
  not not_1 (_74163_1_pin1, _74163_2_pin10);
  not not_2 (_74163_2_pin1, _7421_2_pin6);
  _74163 _74163_6 (
    .pin1(_74163_2_pin1), .pin2(clk), .pin3(1'b0), .pin4(1'b0), .pin5(1'b0), .pin6(1'b0), .pin7(1'b1),
    .pin8(1'b0), .pin9(1'b1), .pin10(_74163_4_pin15), .pin13(y9), .pin14(y8), .pin16(1'b1));  // open: pin11, pin12, pin15
  RS_FF_AS rs_ff_as_1 (.S(_7421_1_pin6), .R(_7421_2_pin6), .Q(_7421_1_pin9));  // open: nQ
  RS_FF_AS rs_ff_as_2 (.S(_7421_1_pin8), .R(_7421_2_pin6), .Q(rs_ff_as_2_q));  // open: nQ
  RS_FF_AS rs_ff_as_3 (.S(_7421_2_pin8), .R(_7421_2_pin6), .Q(rs_ff_as_3_q));  // open: nQ
  Break #(.Cycles(1000000)) break_1 (.brk(_7421_1_pin9));
  RS_FF_AS rs_ff_as_4 (.S(_7411_1_pin12), .R(_74163_2_pin10), .Q(rs_ff_as_4_q));  // open: nQ
  RS_FF_AS rs_ff_as_5 (.S(_7411_1_pin6), .R(_74163_2_pin10), .Q(_7411_1_pin11));  // open: nQ
  RS_FF_AS rs_ff_as_6 (.S(_7411_1_pin8), .R(_74163_2_pin10), .Q(rs_ff_as_6_q));  // open: nQ
  _7486 _7486_1 (
    .pin1(_7411_1_pin11), .pin2(rs_ff_as_6_q), .pin3(_7486_1_pin3), .pin4(rs_ff_as_3_q), .pin5(rs_ff_as_2_q),
    .pin6(_7486_1_pin6), .pin7(1'b0), .pin8(_7486_1_pin8), .pin9(_7421_1_pin9), .pin10(1'b1),
    .pin11(_7486_1_pin11), .pin12(rs_ff_as_4_q), .pin13(1'b1), .pin14(1'b1));
  LED led_1 (.in(_7421_1_pin9));
  LED led_2 (.in(rs_ff_as_2_q));
  LED led_3 (.in(rs_ff_as_3_q));
  LED led_4 (.in(rs_ff_as_4_q));
  LED led_5 (.in(_7411_1_pin11));
  LED led_6 (.in(rs_ff_as_6_q));
  LED led_7 (.in(_7486_1_pin3));
  LED led_8 (.in(_7486_1_pin11));
  LED led_9 (.in(_7486_1_pin6));
  LED led_10 (.in(_7486_1_pin8));
  and and_1 (and_1_out, _7486_1_pin11, _7486_1_pin8);
  // Probe on {y8, y7, y6, y5, y4, y3, y2, y1, y0, q9, q8, q7, q6, q5, q4, q3, q2, q1, q0}
  and and_2 (and_2_out, q0, and_1_out);
  not not_3 (not_3_out, q0);
  and and_3 (and_3_out, not_3_out, and_1_out);
  D_FF d_ff_1 (.D(d_ff_1_nq), .C(clk), .Q(d_ff_1_q), .nQ(d_ff_1_nq));
  RAMDualPort #(.AddrBits(18), .isProgramMemory("true"), .Bits(8)) ramdualport_1 (
    .A({y8, y7, y6, y5, y4, y3, y2, y1, y0, q9, q8, q7, q6, q5, q4, q3, q2, q1}), .Din(8'h1), .str(1'b0),
    .C(d_ff_1_nq), .ld(and_2_out), .D(ramdualport_1_d));
  not not_4 (not_4_out, d_ff_1_nq);
  RAMDualPort #(.AddrBits(18), .isProgramMemory("true"), .Bits(8)) RAM2 (
    .A({y8, y7, y6, y5, y4, y3, y2, y1, y0, q9, q8, q7, q6, q5, q4, q3, q2, q1}), .Din(8'h1), .str(1'b0),
    .C(not_4_out), .ld(and_3_out), .D(RAM2_d));
  Register #(.Bits(8)) register_1 (.D(ramdualport_1_d), .C(d_ff_1_nq), .en(d_ff_1_nq), .Q(register_1_q));
  Register #(.Bits(8)) register_2 (.D(RAM2_d), .C(not_4_out), .en(not_4_out), .Q(register_2_q));
  _74157 _74157_1 (
    .pin1(q0), .pin2(register_1_q[0]), .pin3(register_2_q[0]), .pin4(_74157_1_pin7[0]),
    .pin5(register_1_q[1]), .pin6(register_2_q[1]), .pin7(_74157_1_pin7[1]), .pin8(1'b0),
    .pin9(_74157_1_pin7[2]), .pin10(register_2_q[2]), .pin11(register_1_q[2]), .pin12(_74157_1_pin7[3]),
    .pin13(register_2_q[3]), .pin14(register_1_q[3]), .pin15(1'b0), .pin16(1'b1));
  _74157 _74157_2 (
    .pin1(q0), .pin2(register_1_q[4]), .pin3(register_2_q[4]), .pin4(_74157_1_pin7[4]),
    .pin5(register_1_q[5]), .pin6(register_2_q[5]), .pin7(_74157_1_pin7[5]), .pin8(1'b0),
    .pin9(_74157_1_pin7[6]), .pin10(register_2_q[6]), .pin11(register_1_q[6]), .pin12(_74157_1_pin7[7]),
    .pin13(register_2_q[7]), .pin14(register_1_q[7]), .pin15(1'b0), .pin16(1'b1));

  // Notes on the sheet:
  //   74LS279
  //   480 lines
  //   490 lines
  //   492 lines
  //   525 lines
  //   640 pixels reached
  //   656 pixels reached
  //   752 pixels reached
  //   800 pixels reached
  //   HSYNC
  //   SEND_DATA
  //   VSYNC
endmodule
